// Digital circuit 1bit_register.dig as structural Verilog
module _1bit_register (
  input  Load,
  input  i3,
  input  Clock,
  output A3
);

  wire multiplexer_1_out;

  Multiplexer multiplexer_1 (.sel(Load), .in_0(A3), .in_1(i3), .out(multiplexer_1_out));
  D_FF d_ff_1 (.D(multiplexer_1_out), .C(Clock), .Q(A3));  // open: nQ
endmodule
