// Digital circuit 3vabove.dig as structural Verilog
module _3vabove (
  input  x,
  input  y,
  input  z,
  output F
);

  wire and_1_out, and_2_out, and_3_out, not_1_out, not_2_out, not_3_out;

  not not_1 (not_1_out, x);
  not not_2 (not_2_out, y);
  not not_3 (not_3_out, z);
  and and_1 (and_1_out, x, not_2_out, z);
  and and_2 (and_2_out, x, y, not_3_out);
  and and_3 (and_3_out, x, y, z);
  or or_1 (F, and_1_out, and_2_out, and_3_out);

  // Notes on the sheet:
  //   F=xy’z + xyz’ + xyz
endmodule
