// Digital circuit 4bit3bitmultiplier.dig as structural Verilog
module _4bit3bitmultiplier (
);

  // And and_1 is placed but not wired
  // And and_2 is placed but not wired
  // And and_3 is placed but not wired
  // And and_4 is placed but not wired
  // And and_5 is placed but not wired
  // And and_6 is placed but not wired
  _4bit_adder _4bit_adder_1 ();  // open: C0, A1, A2, A3, A4, B1, B2, B3, B4, S1, S2, S3, S4, C4
  // And and_7 is placed but not wired
  // And and_8 is placed but not wired
endmodule
