// Digital circuit 4bit_adder.dig as structural Verilog
module _4bit_adder (
  input  C0,
  input  B0,
  input  A0,
  input  B1,
  input  A1,
  input  B2,
  input  A2,
  input  B3,
  input  A3,
  output S0,
  output S1,
  output S2,
  output S3,
  output C4
);

  wire full_adder_1_p5, full_adder_2_p5, full_adder_3_p5;

  // full_adder full_adder_1: pin names not known; wires that end beside it: C4, S3, B3, A3, full_adder_1_p5
  // full_adder full_adder_2: pin names not known; wires that end beside it: full_adder_1_p5, S2, B2, A2, full_adder_2_p5
  // full_adder full_adder_3: pin names not known; wires that end beside it: full_adder_2_p5, S1, B1, A1, full_adder_3_p5
  // full_adder full_adder_4: pin names not known; wires that end beside it: full_adder_3_p5, S0, B0, A0, C0
endmodule
