// Digital circuit 4bit_adder_sub.dig as structural Verilog
module _4bit_adder_sub (
  input  A0,
  input  B0,
  input  A1,
  input  B1,
  input  A2,
  input  B2,
  input  A3,
  input  B3,
  input  C0,
  output S0,
  output S1,
  output S2,
  output S3,
  output C4
);

  wire full_adder_1_p4, full_adder_2_p4, full_adder_3_p4, xor_1_out, xor_2_out, xor_3_out, xor_4_out;

  xor xor_1 (xor_1_out, B3, C0);
  // full_adder full_adder_1: pin names not known; wires that end beside it: xor_1_out, A3, C4, full_adder_1_p4, S3
  xor xor_2 (xor_2_out, B2, C0);
  // full_adder full_adder_2: pin names not known; wires that end beside it: xor_2_out, A2, full_adder_1_p4, full_adder_2_p4, S2
  xor xor_3 (xor_3_out, B1, C0);
  // full_adder full_adder_3: pin names not known; wires that end beside it: xor_3_out, A1, full_adder_2_p4, full_adder_3_p4, S1
  xor xor_4 (xor_4_out, B0, C0);
  // full_adder full_adder_4: pin names not known; wires that end beside it: xor_4_out, A0, full_adder_3_p4, C0, S0
endmodule
