// Digital circuit 74181_ALU.dig as structural Verilog
module _74181_ALU (
  input  A0,
  input  A1,
  input  A2,
  input  A3,
  input  B0,
  input  B1,
  input  B2,
  input  B3,
  input  CN,
  input  M,
  input  S0,
  input  S1,
  input  S2,
  input  S3,
  output CN4,
  output A_eq_B,
  output G,
  output F3,
  output F2,
  output F1,
  output F0,
  output P
);

  _74181 _74181_1 (
    .pin1(B0), .pin2(A0), .pin3(S3), .pin4(S2), .pin5(S1), .pin6(S0), .pin7(CN), .pin8(M), .pin9(F0),
    .pin10(F1), .pin11(F2), .pin12(1'b0));  // open: pin13, pin14, pin15, pin16, pin17, pin18, pin19, pin20, pin21, pin22, pin23, pin24
endmodule
