// Digital circuit 74283_4bit_adder.dig as structural Verilog
module _74283_4bit_adder (
  input  A2,
  input  A3,
  input  B1,
  input  B2,
  input  B3,
  input  A1,
  input  A4,
  input  B4,
  input  C0,
  output S1,
  output S3,
  output S4,
  output S2,
  output C4
);

  _74283 _74283_1 (
    .pin1(S2), .pin2(B2), .pin3(A2), .pin4(S1), .pin5(A1), .pin6(B1), .pin7(C0), .pin8(1'b0), .pin9(C4),
    .pin10(S4), .pin11(B4), .pin12(A4), .pin13(S3), .pin14(A3), .pin15(B3), .pin16(1'b1));
endmodule
