// Digital circuit 74hc293_Tflip.dig as structural Verilog
module _74hc293_Tflip (
  input  clk,
  input  _1,
  output A0,
  output A1,
  output A2,
  output A3
);

  wire t_ff_1_nq, t_ff_2_nq, t_ff_3_nq;

  T_FF t_ff_1 (.T(_1), .C(clk), .Q(A0), .nQ(t_ff_1_nq));
  T_FF t_ff_2 (.T(_1), .C(t_ff_1_nq), .Q(A1), .nQ(t_ff_2_nq));
  T_FF t_ff_3 (.T(_1), .C(t_ff_2_nq), .Q(A2), .nQ(t_ff_3_nq));
  T_FF t_ff_4 (.T(_1), .C(t_ff_3_nq), .Q(A3));  // open: nQ

  // Notes on the sheet:
  //   _1: default 1
endmodule
