// Digital circuit 74hc393_counter.dig as structural Verilog
module _74hc393_counter (
  input  clk,
  output A0,
  output A1,
  output A2,
  output A3
);

  wire d_ff_1_nq, d_ff_2_nq, d_ff_3_nq, d_ff_4_nq;

  D_FF d_ff_1 (.D(d_ff_1_nq), .C(clk), .Q(A0), .nQ(d_ff_1_nq));
  D_FF d_ff_2 (.D(d_ff_2_nq), .C(d_ff_1_nq), .Q(A1), .nQ(d_ff_2_nq));
  D_FF d_ff_3 (.D(d_ff_3_nq), .C(d_ff_2_nq), .Q(A2), .nQ(d_ff_3_nq));
  D_FF d_ff_4 (.D(d_ff_4_nq), .C(d_ff_3_nq), .Q(A3), .nQ(d_ff_4_nq));
endmodule
