// Digital circuit ALU_8bit.dig as structural Verilog
module ALU_8bit (
  input  A0,
  input  B0,
  input  A1,
  input  B1,
  input  A2,
  input  B2,
  input  A3,
  input  B3,
  input  M,
  input  A4,
  input  B4,
  input  A5,
  input  B5,
  input  A6,
  input  B6,
  input  A7,
  input  B7,
  output S0,
  output S1,
  output S2,
  output S3,
  output S4,
  output S5,
  output S6,
  output S7,
  output C5
);

  wire full_adder_1_p4, full_adder_2_p4, full_adder_3_p4, full_adder_4_p4, full_adder_5_p4, full_adder_6_p4,
       full_adder_7_p4, xor_1_out, xor_2_out, xor_3_out, xor_4_out, xor_5_out, xor_6_out, xor_7_out,
       xor_8_out;

  xor xor_1 (xor_1_out, B7, M);
  // full_adder full_adder_1: pin names not known; wires that end beside it: xor_1_out, A7, C5, full_adder_1_p4, S7
  xor xor_2 (xor_2_out, B6, M);
  // full_adder full_adder_2: pin names not known; wires that end beside it: xor_2_out, A6, full_adder_1_p4, full_adder_2_p4, S6
  xor xor_3 (xor_3_out, B5, M);
  // full_adder full_adder_3: pin names not known; wires that end beside it: xor_3_out, A5, full_adder_2_p4, full_adder_3_p4, S5
  xor xor_4 (xor_4_out, B4, M);
  // full_adder full_adder_4: pin names not known; wires that end beside it: xor_4_out, A4, full_adder_3_p4, full_adder_4_p4, S4
  xor xor_5 (xor_5_out, B3, M);
  // full_adder full_adder_5: pin names not known; wires that end beside it: xor_5_out, A3, full_adder_4_p4, full_adder_5_p4, S3
  xor xor_6 (xor_6_out, B2, M);
  // full_adder full_adder_6: pin names not known; wires that end beside it: xor_6_out, A2, full_adder_5_p4, full_adder_6_p4, S2
  xor xor_7 (xor_7_out, B1, M);
  // full_adder full_adder_7: pin names not known; wires that end beside it: xor_7_out, A1, full_adder_6_p4, full_adder_7_p4, S1
  xor xor_8 (xor_8_out, B0, M);
  // full_adder full_adder_8: pin names not known; wires that end beside it: xor_8_out, A0, full_adder_7_p4, M, S0
endmodule
