// Digital circuit ALU_EEE207.dig as structural Verilog
// Arithmetic Logical unit.
// Performs all arithmetic operations.
// Used for arithmetic processor instructions as well as for 
// calculating memory addresses.
// {{de Arithmetisch Logische Einheit. 
// Führt alle arithmetischen Operationen durch. 
// Wird sowohl für arithmetische Prozessorbefehle 
// als auch für die Berechnung der Adressen 
// bei der Speicheradressierung verwendet.}}
module ALU_EEE207 (
  input  [15:0] A,
  input  [15:0] B,
  input  [1:0] SC,
  output [15:0] Y,
  output C
);

  wire add_1_c_o, sub_1_c_o;
  wire [15:0] add_1_s, sub_1_s;

  Add #(.Bits(16)) add_1 (.a(A), .b(B), .c_i(SC[0]), .s(add_1_s), .c_o(add_1_c_o));
  Sub #(.Bits(16)) sub_1 (.a(A), .b(B), .c_i(SC[0]), .s(sub_1_s), .c_o(sub_1_c_o));
  Multiplexer #(.Bits(16)) multiplexer_1 (.sel(SC[1]), .in_0(add_1_s), .in_1(sub_1_s), .out(Y));
  Multiplexer multiplexer_2 (.sel(SC[1]), .in_0(add_1_c_o), .in_1(sub_1_c_o), .out(C));

  // Notes on the sheet:
  //   A: first operand
  //   {{de Erster Operand}}
  //   B: second operand
  //   {{de Zweiter Operand}}
  //   Y: result of the operation
  //   {{de Ergebnis der Operation}}
  //   C: Is high if there has been a carry.
  //   {{de Ist High wenn es einen Übertrag gegeben hat.}}
endmodule
