// Digital circuit ALU_EEE213.dig as structural Verilog
module ALU_EEE213 (
  input  M,
  input  [3:0] A,
  input  [3:0] B,
  output C,
  output [3:0] S
);

  wire full_adder_1_p4, full_adder_2_p4, full_adder_3_p4, xor_1_out, xor_2_out, xor_3_out, xor_4_out;

  xor xor_1 (xor_1_out, B[3], M);
  // full_adder full_adder_1: pin names not known; wires that end beside it: xor_1_out, A[3], C, full_adder_1_p4, S[3]
  xor xor_2 (xor_2_out, B[2], M);
  // full_adder full_adder_2: pin names not known; wires that end beside it: xor_2_out, A[2], full_adder_1_p4, full_adder_2_p4, S[2]
  xor xor_3 (xor_3_out, B[1], M);
  // full_adder full_adder_3: pin names not known; wires that end beside it: xor_3_out, A[1], full_adder_2_p4, full_adder_3_p4, S[1]
  xor xor_4 (xor_4_out, B[0], M);
  // full_adder full_adder_4: pin names not known; wires that end beside it: xor_4_out, A[0], full_adder_3_p4, M, S[0]
endmodule
