// Digital circuit AeqB_v2.dig as structural Verilog
module AeqB_v2 (
  input  A,
  input  B,
  output A_gt_B,
  output A_eq_B,
  output A_lt_B
);

  wire and_2_out, and_3_out, not_1_out, not_2_out;

  not not_1 (not_1_out, A);
  not not_2 (not_2_out, B);
  and and_1 (A_gt_B, A, not_2_out);
  and and_2 (and_2_out, not_1_out, not_2_out);
  and and_3 (and_3_out, A, B);
  and and_4 (A_lt_B, not_1_out, B);
  or or_1 (A_eq_B, and_2_out, and_3_out);
endmodule
