// Digital circuit D_latch.dig as structural Verilog
module D_latch (
  input  Enable,
  input  Data,
  output Output
);

  wire nand_1_out, nand_2_out, nand_4_out, not_1_out;

  not not_1 (not_1_out, Data);
  nand nand_1 (nand_1_out, Data, Enable);
  nand nand_2 (nand_2_out, Enable, not_1_out);
  nand nand_3 (Output, nand_1_out, nand_4_out);
  nand nand_4 (nand_4_out, Output, nand_2_out);
endmodule
