// Digital circuit Dlatch.dig as structural Verilog
module Dlatch (
  input  D,
  input  En,
  output Q
);

  wire nand_1_out, nand_2_out, nand_4_out, not_1_out;

  not not_1 (not_1_out, D);
  nand nand_1 (nand_1_out, D, En);
  nand nand_2 (nand_2_out, En, not_1_out);
  nand nand_3 (Q, nand_1_out, nand_4_out);
  nand nand_4 (nand_4_out, Q, nand_2_out);
endmodule
