// Digital circuit EEE213_q2.dig as structural Verilog
module EEE213_q2 (
  input  [2:0] _101,
  output A_eq,
  output B_eq,
  output C_eq,
  output D_eq,
  output E_eq,
  output F_eq,
  output G_eq,
  output H_eq
);

  Decoder #(.Selector_Bits(3)) decoder_1 (
    .sel(_101), .out_0(A_eq), .out_1(B_eq), .out_2(C_eq), .out_3(D_eq), .out_4(E_eq), .out_5(F_eq),
    .out_6(G_eq), .out_7(H_eq));
endmodule
