// Digital circuit MCU_EEE13.dig as structural Verilog
module MCU_EEE13 (
  input  Clock
);

  wire and_1_out, and_2_out, and_3_out, and_4_out, nand_1_out, or_1_out;
  wire [3:0] alu_eee213_1_s, multiplexer_1_out, pc_eee207_1_pc, RA_q, RB_q, rom_1_d;
  wire [11:4] rom_1_d_2;

  PC_EEE207 pc_eee207_1 (.C(Clock), .PC(pc_eee207_1_pc));  // open: Next
  ROM #(.AddrBits(4), .isProgramMemory("true"), .Bits(12)) rom_1 (
    .A(pc_eee207_1_pc), .sel(1'b1), .D({rom_1_d_2, rom_1_d}));
  and and_1 (and_1_out, ~rom_1_d_2[11], ~rom_1_d_2[10], ~rom_1_d_2[9], rom_1_d_2[8]);  // And
  and and_2 (and_2_out, rom_1_d_2[11], rom_1_d_2[10]);
  and and_3 (and_3_out, ~rom_1_d_2[11], ~rom_1_d_2[10], rom_1_d_2[9], ~rom_1_d_2[8]);  // And
  nand nand_1 (nand_1_out, rom_1_d_2[11], rom_1_d_2[10], ~rom_1_d_2[9], ~rom_1_d_2[8]);  // NAnd
  and and_4 (and_4_out, ~rom_1_d_2[11], rom_1_d_2[10], ~rom_1_d_2[9], rom_1_d_2[8]);  // And
  or or_1 (or_1_out, and_1_out, and_2_out);
  Multiplexer #(.Bits(4)) multiplexer_1 (
    .sel(and_1_out), .in_0(alu_eee213_1_s), .in_1(rom_1_d), .out(multiplexer_1_out));
  Register #(.Bits(4)) RA (.D(multiplexer_1_out), .C(Clock), .en(or_1_out), .Q(RA_q));
  Register #(.Bits(4)) RB (.D(rom_1_d), .C(Clock), .en(and_3_out), .Q(RB_q));
  ALU_EEE213 alu_eee213_1 (.M(nand_1_out), .A(RA_q), .B(RB_q), .S(alu_eee213_1_s));  // open: C
  RAMSinglePort #(.AddrBits(4), .Bits(4), .Addr_Bits(16)) mem (
    .A(4'b0000), .str(and_4_out), .C(Clock), .ld(1'b0), .D(RA_q));

  // Other names for the same wires on the sheet: C = Clock

  // Notes on the sheet:
  //   Clock: Hz: 2147483647
  //   contents of rom_1 (hex, n*v repeats v):
  //   103,202,c00,c00,d00,580
endmodule
