// Digital circuit MCU_EEE20_v2.dig as structural Verilog
module MCU_EEE20_v2 (
  input  Clock
);

  wire and_1_out, and_2_out, xnor_1_out;
  wire [15:0] alu_eee207v2_1_y, multiplexer_1_out, pc_eee207_1_pc, RA_q, RB_q, rom_1_d;
  wire [31:16] rom_1_d_2;

  PC_EEE207 pc_eee207_1 (.C(Clock), .PC(pc_eee207_1_pc));  // open: Next
  ROM #(.AddrBits(16), .isProgramMemory("true"), .Bits(32)) rom_1 (
    .A(pc_eee207_1_pc), .sel(1'b1), .D({rom_1_d_2, rom_1_d}));
  Multiplexer #(.Bits(16)) multiplexer_1 (
    .sel(rom_1_d_2[19]), .in_0(alu_eee207v2_1_y), .in_1(rom_1_d), .out(multiplexer_1_out));
  xnor xnor_1 (xnor_1_out, rom_1_d_2[18], rom_1_d_2[19]);
  and and_1 (and_1_out, ~rom_1_d_2[18], rom_1_d_2[19]);  // And
  Register #(.Bits(16)) RA (.D(multiplexer_1_out), .C(Clock), .en(xnor_1_out), .Q(RA_q));
  Register #(.Bits(16)) RB (.D(rom_1_d), .C(Clock), .en(and_1_out), .Q(RB_q));
  and and_2 (and_2_out, rom_1_d_2[18], ~rom_1_d_2[19]);  // And
  ALU_EEE207V2 alu_eee207v2_1 (.A(RA_q), .B(RB_q), .SC(rom_1_d_2[17:16]), .Y(alu_eee207v2_1_y));  // open: C
  RAMSinglePort #(.AddrBits(16), .Bits(16), .Addr_Bits(16)) mem (
    .A({16{1'b0}}), .str(and_2_out), .C(Clock), .ld(1'b0), .D(RA_q));

  // Other names for the same wires on the sheet: C = Clock

  // Notes on the sheet:
  //   Clock: Hz: 2147483647
  //   contents of rom_1 (hex, n*v repeats v):
  //   c0004,80002,ffff,2ffff,4ffff
endmodule
