// Digital circuit MCU_EEE20_v3.dig as structural Verilog
module MCU_EEE20_v3 (
  input  Clock
);

  wire and_1_out, and_2_out, and_3_out, and_4_out;
  wire [15:0] alu_eee207v2_1_y, multiplexer_1_out, pc_eee207_1_pc, RA_q, RB_q, rom_1_d;
  wire [31:16] rom_1_d_2;

  PC_EEE207 pc_eee207_1 (.C(Clock), .PC(pc_eee207_1_pc));  // open: Next
  ROM #(.AddrBits(16), .isProgramMemory("true"), .Bits(32)) rom_1 (
    .A(pc_eee207_1_pc), .sel(1'b1), .D({rom_1_d_2, rom_1_d}));
  and and_1 (and_1_out, ~rom_1_d_2[18], rom_1_d_2[19], rom_1_d_2[20]);  // And
  and and_2 (and_2_out, rom_1_d_2[19], rom_1_d_2[20]);
  and and_3 (and_3_out, rom_1_d_2[18], ~rom_1_d_2[19], rom_1_d_2[20]);  // And
  and and_4 (and_4_out, ~rom_1_d_2[18], ~rom_1_d_2[19], rom_1_d_2[20]);  // And
  Multiplexer #(.Bits(16)) multiplexer_1 (
    .sel(and_1_out), .in_0(alu_eee207v2_1_y), .in_1(rom_1_d), .out(multiplexer_1_out));
  Register #(.Bits(16)) RA (.D(multiplexer_1_out), .C(Clock), .en(and_2_out), .Q(RA_q));
  Register #(.Bits(16)) RB (.D(rom_1_d), .C(Clock), .en(and_3_out), .Q(RB_q));
  ALU_EEE207V2 alu_eee207v2_1 (.A(RA_q), .B(RB_q), .SC(rom_1_d_2[17:16]), .Y(alu_eee207v2_1_y));  // open: C
  RAMSinglePort #(.AddrBits(16), .Bits(16), .Addr_Bits(16)) mem (
    .A({16{1'b0}}), .str(and_4_out), .C(Clock), .ld(1'b0), .D(RA_q));

  // Other names for the same wires on the sheet: C = Clock

  // Notes on the sheet:
  //   Clock: Hz: 2147483647
  //   contents of rom_1 (hex, n*v repeats v):
  //   180004,140002,1cffff,1effff,10ffff
endmodule
