// Digital circuit MCU_EEE213.dig as structural Verilog
module MCU_EEE213 (
  input  Clock
);

  wire decoder_1_out_1, decoder_1_out_2, decoder_1_out_3, decoder_1_out_4, decoder_1_out_5, or_1_out;
  wire [3:0] alu_eee213_1_s, multiplexer_1_out, pc_eee207_1_pc, RA_q, RB_q, rom_1_d, rom_1_d_3;
  wire [7:4] rom_1_d_2;

  PC_EEE207 pc_eee207_1 (.C(Clock), .PC(pc_eee207_1_pc));  // open: Next
  ROM #(.AddrBits(4), .isProgramMemory("true"), .Bits(12)) rom_1 (
    .A(pc_eee207_1_pc), .sel(1'b1), .D({rom_1_d_3, rom_1_d_2, rom_1_d}));
  Decoder #(.Selector_Bits(4)) decoder_1 (
    .sel(rom_1_d_3), .out_1(decoder_1_out_1), .out_2(decoder_1_out_2), .out_3(decoder_1_out_3),
    .out_4(decoder_1_out_4), .out_5(decoder_1_out_5));  // open: out_0, out_6, out_7, out_8, out_9, out_10, out_11, out_12, out_13, out_14, out_15
  Multiplexer #(.Bits(4)) multiplexer_1 (
    .sel(decoder_1_out_1), .in_0(alu_eee213_1_s), .in_1(rom_1_d), .out(multiplexer_1_out));
  or or_1 (or_1_out, decoder_1_out_1, decoder_1_out_3, decoder_1_out_4);
  Register #(.Bits(4)) RA (.D(multiplexer_1_out), .C(Clock), .en(or_1_out), .Q(RA_q));
  Register #(.Bits(4)) RB (.D(rom_1_d), .C(Clock), .en(decoder_1_out_2), .Q(RB_q));
  ALU_EEE213 alu_eee213_1 (.M(decoder_1_out_4), .A(RA_q), .B(RB_q), .S(alu_eee213_1_s));  // open: C
  RAMSinglePort #(.AddrBits(4), .Bits(4), .Addr_Bits(16)) mem (
    .A(4'b0000), .str(decoder_1_out_5), .C(Clock), .ld(1'b0), .D(RA_q));

  // Other names for the same wires on the sheet: C = Clock

  // Notes on the sheet:
  //   Clock: Hz: 2147483647
  //   contents of rom_1 (hex, n*v repeats v):
  //   103,202,300,300,400,500
endmodule
