// Digital circuit MŞDTERM Q1.dig as structural Verilog
module \MŞDTERM_Q1  (
  input  [2:0] \input ,
  output A,
  output B,
  output C,
  output D,
  output E,
  output F,
  output G,
  output H
);

  Decoder #(.Selector_Bits(3)) decoder_1 (
    .sel(\input ), .out_0(A), .out_1(B), .out_2(C), .out_3(D), .out_4(E), .out_5(F), .out_6(G), .out_7(H));

  // Notes on the sheet:
  //   input: default 5
endmodule
