// Digital circuit PC_EEE207.dig as structural Verilog
module PC_EEE207 (
  input  C,
  output [3:0] PC,
  output [3:0] Next
);

  wire Reset_out;

  Register #(.Bits(4), .isProgramCounter("true")) u_PC (.D(Next), .C(~C), .en(Reset_out), .Q(PC));
  Reset Reset (.out(Reset_out));
  Add #(.Bits(4)) Add_One (.a(PC), .b(4'b0001), .c_i(1'b0), .s(Next));  // open: c_o

  // Notes on the sheet:
  //   PC: Programm Counter
  //   {{de Programmzähler}}
  //   Next: Address of the next instruction to execute.
  //   {{de Adresse des nächsten auszuführenden Befehls.}}
endmodule
