// Digital circuit RAM_4x4.dig as structural Verilog
module RAM_4x4 (
  input  i3,
  input  i2,
  input  i1,
  input  i0,
  input  W_R,
  input  [1:0] A,
  output Q0,
  output Q1,
  output Q2,
  output Q3
);

  wire decoder_1_out_0, decoder_1_out_1, decoder_1_out_2, decoder_1_out_3, memory_cell_1_o, memory_cell_2_o,
       memory_cell_3_o, memory_cell_4_o, memory_cell_5_o, memory_cell_6_o, memory_cell_7_o, memory_cell_8_o,
       memory_cell_9_o, memory_cell_10_o, memory_cell_11_o, memory_cell_12_o, memory_cell_13_o,
       memory_cell_14_o, memory_cell_15_o, memory_cell_16_o;

  Decoder #(.Selector_Bits(2)) decoder_1 (
    .sel(A), .out_0(decoder_1_out_0), .out_1(decoder_1_out_1), .out_2(decoder_1_out_2),
    .out_3(decoder_1_out_3));
  memory_cell memory_cell_1 (.i(i3), .W_R(W_R), .S(decoder_1_out_0), .O(memory_cell_1_o));
  memory_cell memory_cell_2 (.i(i3), .W_R(W_R), .S(decoder_1_out_1), .O(memory_cell_2_o));
  memory_cell memory_cell_3 (.i(i3), .W_R(W_R), .S(decoder_1_out_2), .O(memory_cell_3_o));
  memory_cell memory_cell_4 (.i(i3), .W_R(W_R), .S(decoder_1_out_3), .O(memory_cell_4_o));
  or or_1 (Q3, memory_cell_1_o, memory_cell_2_o, memory_cell_3_o, memory_cell_4_o);
  memory_cell memory_cell_5 (.i(i2), .W_R(W_R), .S(decoder_1_out_0), .O(memory_cell_5_o));
  memory_cell memory_cell_6 (.i(i2), .W_R(W_R), .S(decoder_1_out_1), .O(memory_cell_6_o));
  memory_cell memory_cell_7 (.i(i2), .W_R(W_R), .S(decoder_1_out_2), .O(memory_cell_7_o));
  memory_cell memory_cell_8 (.i(i2), .W_R(W_R), .S(decoder_1_out_3), .O(memory_cell_8_o));
  or or_2 (Q2, memory_cell_5_o, memory_cell_6_o, memory_cell_7_o, memory_cell_8_o);
  memory_cell memory_cell_9 (.i(i1), .W_R(W_R), .S(decoder_1_out_0), .O(memory_cell_9_o));
  memory_cell memory_cell_10 (.i(i1), .W_R(W_R), .S(decoder_1_out_1), .O(memory_cell_10_o));
  memory_cell memory_cell_11 (.i(i1), .W_R(W_R), .S(decoder_1_out_2), .O(memory_cell_11_o));
  memory_cell memory_cell_12 (.i(i1), .W_R(W_R), .S(decoder_1_out_3), .O(memory_cell_12_o));
  or or_3 (Q1, memory_cell_9_o, memory_cell_10_o, memory_cell_11_o, memory_cell_12_o);
  memory_cell memory_cell_13 (.i(i0), .W_R(W_R), .S(decoder_1_out_0), .O(memory_cell_13_o));
  memory_cell memory_cell_14 (.i(i0), .W_R(W_R), .S(decoder_1_out_1), .O(memory_cell_14_o));
  memory_cell memory_cell_15 (.i(i0), .W_R(W_R), .S(decoder_1_out_2), .O(memory_cell_15_o));
  memory_cell memory_cell_16 (.i(i0), .W_R(W_R), .S(decoder_1_out_3), .O(memory_cell_16_o));
  or or_4 (Q0, memory_cell_13_o, memory_cell_14_o, memory_cell_15_o, memory_cell_16_o);
endmodule
