// Digital circuit RAM_v2.dig as structural Verilog
// A memory combining ROM and RAM.
// The addresses 0-0x7FFF are mapped to a ROM, the 
// addresses 0x8000-0xFFFF to a RAM component. 
// Thus, ROM and RAM can be found in the same 
// address space.
// {{de Ein Speicher kombiniert aus ROM und RAM.
// Die Adressen 0-0x7FFF werden auf ein ROM 
// abgebildet, die Adressen 0x8000-0xFFFF auf einen
// RAM-Baustein. Somit finden sich ROM und RAM im
// selben Adressraum.}}
module RAM_v2 (
  input  [15:0] A,
  input  WRITE,
  input  C,
  input  READ,
  input  [15:0] DATA,
  input  BUS,
  output [15:0] D
);

  assign D = BUS ? DATA : 16'bz;  // Driver driver_1
  RAMSinglePort #(.AddrBits(16), .Bits(16), .Addr_Bits(15)) ramsingleport_1 (
    .A(A), .str(WRITE), .C(C), .ld(READ), .D(D));

  // Notes on the sheet:
  //   A: address bus
  //   {{de Der Adressbus}}, default 16
  //   WRITE: store data
  //   {{de Daten speichern}}
  //   READ: read memory
  //   {{de Speicher lesen}}
  //   DATA: address bus
  //   {{de Der Adressbus}}, default 18
  //   BUS: default 16
endmodule
