// Digital circuit ROM_2x2.dig as structural Verilog
module ROM_2x2 (
  input  [1:0] address,
  input  sel,
  output [1:0] out_2
);

  ROM #(.Bits(2)) rom_1 (.A(address), .sel(sel), .D(out_2));

  // Notes on the sheet:
  //   sel: default 1
  //   contents of rom_1 (hex, n*v repeats v):
  //   0,1,1,2
endmodule
