// Digital circuit ROM_v2.dig as structural Verilog
module ROM_v2 (
  input  [15:0] A,
  input  SEL,
  output [15:0] out_1
);

  ROM #(.AddrBits(16), .Bits(16)) rom_1 (.A(A), .sel(SEL), .D(out_1));

  // Notes on the sheet:
  //   A: default 1
  //   SEL: default 1
  //   contents of rom_1 (hex, n*v repeats v):
  //   1234,5678,9999
endmodule
