// Digital circuit SR_NAND_Latch.dig as structural Verilog
module SR_NAND_Latch (
  input  R,
  input  S,
  output Q
);

  wire nand_1_out;

  nand nand_1 (nand_1_out, R, Q);
  nand nand_2 (Q, nand_1_out, S);
endmodule
