// Digital circuit above3V_table.dig as structural Verilog
module above3V_table (
  input  x,
  input  y_2,
  input  z,
  output Y
);

  wire and_1_out, and_2_out;

  and and_1 (and_1_out, x, z);
  and and_2 (and_2_out, x, y_2);
  or or_1 (Y, and_1_out, and_2_out);
endmodule
