// Digital circuit above3V_v2.dig as structural Verilog
module above3V_v2 (
  input  x,
  input  y_2,
  input  z,
  output Y
);

  wire and_1_out, and_2_out, and_3_out, not_1_out, not_2_out;

  not not_1 (not_1_out, y_2);
  not not_2 (not_2_out, z);
  and and_1 (and_1_out, x, not_1_out, z);
  and and_2 (and_2_out, x, y_2, not_2_out);
  and and_3 (and_3_out, x, y_2, z);
  or or_1 (Y, and_1_out, and_2_out, and_3_out);
endmodule
