// Digital circuit above5.dig as structural Verilog
module above5 (
  input  x,
  input  y,
  input  z,
  output F
);

  wire and_1_out, and_2_out;

  and and_1 (and_1_out, x, z);
  and and_2 (and_2_out, x, y);
  or or_1 (F, and_1_out, and_2_out);
endmodule
