// Digital circuit addsub.dig as structural Verilog
module addsub (
  input  in_5,
  input  in_6,
  input  in_7,
  input  in_8,
  input  in_9,
  input  in_10,
  output out_1,
  output out_2,
  output out_3,
  output out_4
);

  Add add_1 (.a(in_5), .b(in_6), .c_i(in_7), .s(out_1), .c_o(out_2));
  Sub sub_1 (.a(in_8), .b(in_9), .c_i(in_10), .s(out_3), .c_o(out_4));
endmodule
