// Digital circuit catcheven.dig as structural Verilog
module catcheven (
  input  x,
  input  y,
  input  z,
  output F
);

  wire and_1_out, and_2_out, and_3_out, and_4_out, not_1_out, not_2_out, not_3_out;

  not not_1 (not_1_out, x);
  not not_2 (not_2_out, y);
  not not_3 (not_3_out, z);
  and and_1 (and_1_out, not_1_out, not_2_out, z);
  and and_2 (and_2_out, not_1_out, y, z);
  and and_3 (and_3_out, x, not_2_out, z);
  and and_4 (and_4_out, x, y, z);
  or or_1 (F, and_1_out, and_2_out, and_3_out, and_4_out);

  // Notes on the sheet:
  //   F=x’y’z + x’yz + xy’z + xyx
endmodule
