// Digital circuit comparator.dig as structural Verilog
module comparator (
  input  A3,
  input  B3,
  input  A2,
  input  B2,
  input  A1,
  input  B1,
  input  A0,
  input  B0,
  output A_eq_B
);

  wire xnor_1_out, xnor_2_out, xnor_3_out, xnor_4_out;

  xnor xnor_1 (xnor_1_out, A3, B3);
  xnor xnor_2 (xnor_2_out, A2, B2);
  xnor xnor_3 (xnor_3_out, A1, B1);
  xnor xnor_4 (xnor_4_out, A0, B0);
  // And and_1 has open pins: In_1=xnor_1_out, In_2=open, out=open
  // And and_2 has open pins: In_1=xnor_1_out, In_2=open, out=open
  // And and_3 has open pins: In_1=xnor_1_out, In_2=xnor_2_out, In_3=open, out=open
  // And and_4 has open pins: In_1=xnor_1_out, In_2=xnor_2_out, In_3=open, out=open
  // And and_5 has open pins: In_1=xnor_1_out, In_2=xnor_2_out, In_3=open, In_4=open, out=open
  // And and_6 has open pins: In_1=xnor_1_out, In_2=xnor_2_out, In_3=open, In_4=open, out=open
  and and_7 (A_eq_B, xnor_1_out, xnor_2_out, xnor_4_out);  // open: In_3
endmodule
