// Digital circuit d fli flop en.dig as structural Verilog
module d_fli_flop_en (
  input  D,
  input  Clk,
  input  Clr,
  input  Set,
  output Q
);

  D_FF_AS d_ff_as_1 (.Set(Set), .D(D), .C(Clk), .Clr(Clr), .Q(Q));  // open: nQ
endmodule
