// Digital circuit dflipflop_1bit.dig as structural Verilog
module dflipflop_1bit (
  input  Load,
  input  Data,
  input  Clk,
  output Register
);

  wire multiplexer_1_out;

  Multiplexer multiplexer_1 (.sel(Load), .in_0(Register), .in_1(Data), .out(multiplexer_1_out));
  D_FF d_ff_1 (.D(multiplexer_1_out), .C(Clk), .Q(Register));  // open: nQ
endmodule
