// Digital circuit dflipflop_register.dig as structural Verilog
module dflipflop_register (
  input  D,
  input  Clk,
  input  En,
  output Q
);

  wire and_1_out, and_2_out, not_1_out, or_1_out;

  and and_1 (and_1_out, Q, not_1_out);
  not not_1 (not_1_out, En);
  and and_2 (and_2_out, D, En);
  or or_1 (or_1_out, and_1_out, and_2_out);
  D_FF d_ff_1 (.D(or_1_out), .C(Clk), .Q(Q));  // open: nQ
endmodule
