// Digital circuit doorlock.dig as structural Verilog
module doorlock (
  input  _0,
  input  _1,
  input  _2,
  input  _3,
  input  _4,
  input  _5,
  input  _6,
  input  _7,
  input  _8,
  input  _9,
  input  [9:0] num1,
  input  [9:0] num2,
  input  [9:0] num3,
  input  _1_2,
  input  _0_2,
  output lock
);

  wire and_1_out, and_2_out, comparator_1_eq, comparator_2_eq, comparator_3_eq, or_1_out;
  wire [9:0] d_ff_1_q, d_ff_2_q, d_ff_3_q;

  or or_1 (or_1_out, _0, _1, _2, _3, _4, _5, _6, _7, _8, _9);
  D_FF #(.Bits(10)) d_ff_1 (.D({_9, _8, _7, _6, _5, _4, _3, _2, _1, _0}), .C(or_1_out), .Q(d_ff_1_q));  // open: nQ
  Comparator #(.Bits(10)) comparator_1 (.a(num1), .b(d_ff_1_q), .eq(comparator_1_eq));  // open: gt, lt
  D_FF #(.Bits(10)) d_ff_2 (.D(d_ff_1_q), .C(or_1_out), .Q(d_ff_2_q));  // open: nQ
  Comparator #(.Bits(10)) comparator_2 (.a(num2), .b(d_ff_2_q), .eq(comparator_2_eq));  // open: gt, lt
  and and_1 (and_1_out, comparator_1_eq, comparator_2_eq);
  D_FF #(.Bits(10)) d_ff_3 (.D(d_ff_2_q), .C(or_1_out), .Q(d_ff_3_q));  // open: nQ
  Comparator #(.Bits(10)) comparator_3 (.a(num3), .b(d_ff_3_q), .eq(comparator_3_eq));  // open: gt, lt
  and and_2 (and_2_out, and_1_out, comparator_3_eq);
  Multiplexer multiplexer_1 (.sel(and_2_out), .in_0(_1_2), .in_1(_0_2), .out(lock));

  // Notes on the sheet:
  //   num1: default 8
  //   num2: default 4
  //   num3: default 2
  //   _1_2: default 1
endmodule
