// Digital circuit fourbitcounter.dig as structural Verilog
module fourbitcounter (
  input  Input,
  output Q1,
  output Q2,
  output Q3,
  output Q4
);

  wire d_ff_1_nq, d_ff_1_q, d_ff_2_nq, d_ff_2_q, d_ff_3_nq, d_ff_3_q, d_ff_4_nq, d_ff_4_q;

  D_FF d_ff_1 (.D(d_ff_1_nq), .C(Input), .Q(d_ff_1_q), .nQ(d_ff_1_nq));
  D_FF d_ff_2 (.D(d_ff_2_nq), .C(d_ff_1_q), .Q(d_ff_2_q), .nQ(d_ff_2_nq));
  D_FF d_ff_3 (.D(d_ff_3_nq), .C(d_ff_2_q), .Q(d_ff_3_q), .nQ(d_ff_3_nq));
  D_FF d_ff_4 (.D(d_ff_4_nq), .C(d_ff_3_q), .Q(d_ff_4_q), .nQ(d_ff_4_nq));
  not not_1 (Q1, d_ff_1_q);
  not not_2 (Q2, d_ff_2_q);
  not not_3 (Q3, d_ff_3_q);
  not not_4 (Q4, d_ff_4_q);
endmodule
