// Digital circuit fourbitmux register.dig as structural Verilog
module fourbitmux_register (
  input  Enable,
  input  i0,
  input  i1,
  input  i2,
  input  i3,
  input  Clock,
  output A0,
  output A1,
  output A2,
  output A3
);

  wire multiplexer_1_out, multiplexer_2_out, multiplexer_3_out, multiplexer_4_out;

  Multiplexer multiplexer_1 (.sel(Enable), .in_0(A0), .in_1(i0), .out(multiplexer_1_out));
  Multiplexer multiplexer_2 (.sel(Enable), .in_0(A1), .in_1(i1), .out(multiplexer_2_out));
  Multiplexer multiplexer_3 (.sel(Enable), .in_0(A2), .in_1(i2), .out(multiplexer_3_out));
  Multiplexer multiplexer_4 (.sel(Enable), .in_0(A3), .in_1(i3), .out(multiplexer_4_out));
  D_FF d_ff_1 (.D(multiplexer_1_out), .C(Clock), .Q(A0));  // open: nQ
  D_FF d_ff_2 (.D(multiplexer_2_out), .C(Clock), .Q(A1));  // open: nQ
  D_FF d_ff_3 (.D(multiplexer_3_out), .C(Clock), .Q(A2));  // open: nQ
  D_FF d_ff_4 (.D(multiplexer_4_out), .C(Clock), .Q(A3));  // open: nQ
endmodule
