// Digital circuit fourbitparallelregister.dig as structural Verilog
module fourbitparallelregister (
  input  Load,
  input  i0,
  input  i1,
  input  i2,
  input  i3,
  input  Clock,
  output A0,
  output A1,
  output A2,
  output A3
);

  wire and_1_out, and_2_out, and_3_out, and_4_out, and_5_out, and_6_out, and_7_out, and_8_out, not_1_out,
       not_2_out, or_1_out, or_2_out, or_3_out, or_4_out;

  not not_1 (not_1_out, Load);
  not not_2 (not_2_out, not_1_out);
  and and_1 (and_1_out, A0, not_1_out);
  and and_2 (and_2_out, i0, not_2_out);
  and and_3 (and_3_out, A1, not_1_out);
  and and_4 (and_4_out, i1, not_2_out);
  and and_5 (and_5_out, A2, not_1_out);
  and and_6 (and_6_out, i2, not_2_out);
  and and_7 (and_7_out, A3, not_1_out);
  and and_8 (and_8_out, i3, not_2_out);
  or or_1 (or_1_out, and_1_out, and_2_out);
  or or_2 (or_2_out, and_3_out, and_4_out);
  or or_3 (or_3_out, and_5_out, and_6_out);
  or or_4 (or_4_out, and_7_out, and_8_out);
  D_FF d_ff_1 (.D(or_1_out), .C(Clock), .Q(A0));  // open: nQ
  D_FF d_ff_2 (.D(or_2_out), .C(Clock), .Q(A1));  // open: nQ
  D_FF d_ff_3 (.D(or_3_out), .C(Clock), .Q(A2));  // open: nQ
  D_FF d_ff_4 (.D(or_4_out), .C(Clock), .Q(A3));  // open: nQ
endmodule
