// Digital circuit full_adder_v10.dig as structural Verilog
module full_adder_v10 (
  input  C0,
  input  x,
  input  y,
  output S,
  output C1
);

  wire half_adder_1_c, half_adder_1_s, half_adder_2_c;

  half_adder half_adder_1 (.x(x), .y(y), .S(half_adder_1_s), .C(half_adder_1_c));
  half_adder half_adder_2 (.x(half_adder_1_s), .y(C0), .S(S), .C(half_adder_2_c));
  or or_1 (C1, half_adder_2_c, half_adder_1_c);
endmodule
