// Digital circuit fulladder from truth.dig as structural Verilog
module fulladder_from_truth (
  input  X,
  input  Y,
  input  Z,
  output C,
  output S
);

  wire and_1_out, and_2_out, and_3_out, and_4_out, and_5_out, and_6_out, and_7_out, not_1_out, not_2_out,
       not_3_out;

  not not_1 (not_1_out, X);
  not not_2 (not_2_out, Y);
  not not_3 (not_3_out, Z);
  and and_1 (and_1_out, X, Z);
  and and_2 (and_2_out, X, Y);
  and and_3 (and_3_out, Y, Z);
  and and_4 (and_4_out, not_1_out, not_2_out, Z);
  and and_5 (and_5_out, not_1_out, Y, not_3_out);
  and and_6 (and_6_out, X, not_2_out, not_3_out);
  and and_7 (and_7_out, X, Y, Z);
  or or_1 (C, and_1_out, and_2_out, and_3_out);
  or or_2 (S, and_4_out, and_5_out, and_6_out, and_7_out);
endmodule
