// Digital circuit function_to_logic.dig as structural Verilog
module function_to_logic (
  input  x,
  input  y_2,
  input  z,
  output Y
);

  wire and_1_out, and_2_out, not_1_out;

  not not_1 (not_1_out, x);
  and and_1 (and_1_out, x, z);
  and and_2 (and_2_out, not_1_out, y_2);
  or or_1 (Y, and_1_out, and_2_out);
endmodule
