// Digital circuit function_to_logic_nand.dig as structural Verilog
module function_to_logic_nand (
  input  x,
  input  y_2,
  input  z,
  output Y
);

  wire nand_1_out, nand_2_out, not_1_out;

  not not_1 (not_1_out, x);
  nand nand_1 (nand_1_out, not_1_out, y_2);
  nand nand_2 (nand_2_out, x, z);
  nand nand_3 (Y, nand_1_out, nand_2_out);
endmodule
