// Digital circuit logic_gates.dig as structural Verilog
module logic_gates (
  input  X,
  input  Y,
  output A,
  output B,
  output C,
  output E,
  output F,
  output D
);

  and and_1 (A, X, Y);
  nand nand_1 (B, X, Y);
  or or_1 (C, X, Y);
  nor nor_1 (D, X, Y);
  xor xor_1 (E, X, Y);
  xnor xnor_1 (F, X, Y);
endmodule
