// Digital circuit lut4.dig as structural Verilog
module lut4 (
  input  T0,
  input  A1,
  input  A2,
  input  A3,
  input  A0,
  input  T1,
  input  T2,
  input  T3,
  input  T4,
  input  T5,
  input  T6,
  input  T7,
  input  T8,
  input  T9,
  input  T10,
  input  T11,
  input  T12,
  input  T13,
  input  T14,
  input  T15,
  output S
);

  wire multiplexer_1_out, multiplexer_2_out, multiplexer_3_out, multiplexer_4_out, multiplexer_5_out,
       multiplexer_6_out, multiplexer_7_out, multiplexer_8_out, multiplexer_9_out, multiplexer_10_out,
       multiplexer_11_out, multiplexer_12_out, multiplexer_13_out, multiplexer_14_out;

  Multiplexer multiplexer_1 (.sel(A3), .in_0(T0), .in_1(T1), .out(multiplexer_1_out));
  Multiplexer multiplexer_2 (.sel(A3), .in_0(T2), .in_1(T3), .out(multiplexer_2_out));
  Multiplexer multiplexer_3 (.sel(A3), .in_0(T4), .in_1(T5), .out(multiplexer_3_out));
  Multiplexer multiplexer_4 (.sel(A3), .in_0(T6), .in_1(T7), .out(multiplexer_4_out));
  Multiplexer multiplexer_5 (.sel(A3), .in_0(T8), .in_1(T9), .out(multiplexer_5_out));
  Multiplexer multiplexer_6 (.sel(A3), .in_0(T10), .in_1(T11), .out(multiplexer_6_out));
  Multiplexer multiplexer_7 (.sel(A3), .in_0(T12), .in_1(T13), .out(multiplexer_7_out));
  Multiplexer multiplexer_8 (.sel(A3), .in_0(T14), .in_1(T15), .out(multiplexer_8_out));
  Multiplexer multiplexer_9 (.sel(A2), .in_0(multiplexer_1_out), .in_1(multiplexer_2_out), .out(multiplexer_9_out));
  Multiplexer multiplexer_10 (.sel(A2), .in_0(multiplexer_3_out), .in_1(multiplexer_4_out), .out(multiplexer_10_out));
  Multiplexer multiplexer_11 (.sel(A2), .in_0(multiplexer_5_out), .in_1(multiplexer_6_out), .out(multiplexer_11_out));
  Multiplexer multiplexer_12 (.sel(A2), .in_0(multiplexer_7_out), .in_1(multiplexer_8_out), .out(multiplexer_12_out));
  Multiplexer multiplexer_13 (.sel(A1), .in_0(multiplexer_9_out), .in_1(multiplexer_10_out), .out(multiplexer_13_out));
  Multiplexer multiplexer_14 (.sel(A1), .in_0(multiplexer_11_out), .in_1(multiplexer_12_out), .out(multiplexer_14_out));
  Multiplexer multiplexer_15 (.sel(A0), .in_0(multiplexer_13_out), .in_1(multiplexer_14_out), .out(S));
endmodule
