// Digital circuit memory_cell.dig as structural Verilog
module memory_cell (
  input  i,
  input  W_R,
  input  S,
  output O
);

  wire and_1_out, and_2_out, not_1_out, not_2_out, rs_ff_as_1_q;

  not not_1 (not_1_out, i);
  and and_1 (and_1_out, S, not_2_out, i);
  and and_2 (and_2_out, S, not_2_out, not_1_out);
  not not_2 (not_2_out, W_R);
  RS_FF_AS rs_ff_as_1 (.S(and_1_out), .R(and_2_out), .Q(rs_ff_as_1_q));  // open: nQ
  and and_3 (O, S, rs_ff_as_1_q, W_R);
endmodule
