// Digital circuit midterm_2to4decoder.dig as structural Verilog
module midterm_2to4decoder (
  input  A,
  input  B,
  output Y3,
  output Y0,
  output Y1,
  output Y2
);

  wire not_1_out, not_2_out, not_3_out, not_4_out, not_5_out, not_6_out;

  not not_1 (not_1_out, A);
  not not_2 (not_2_out, B);
  not not_3 (not_3_out, not_1_out);
  not not_4 (not_4_out, not_2_out);
  not not_5 (not_5_out, not_3_out);
  not not_6 (not_6_out, not_4_out);
  nand nand_1 (Y3, not_3_out, not_4_out);
  nand nand_2 (Y2, not_5_out, not_4_out);
  nand nand_3 (Y1, not_3_out, not_6_out);
  nand nand_4 (Y0, not_5_out, not_6_out);
endmodule
