// Digital circuit mux2to1_midterm.dig as structural Verilog
module mux2to1_midterm (
  input  X,
  input  Y,
  input  Z,
  output F
);

  Multiplexer multiplexer_1 (.sel(Z), .in_0(X), .in_1(Y), .out(F));
endmodule
