// Digital circuit mux_truth_2bit.dig as structural Verilog
module mux_truth_2bit (
  input  T1,
  input  T2,
  input  T3,
  input  T4,
  input  A,
  input  B,
  output F
);

  wire multiplexer_1_out, multiplexer_2_out;

  Multiplexer multiplexer_1 (.sel(B), .in_0(T1), .in_1(T2), .out(multiplexer_1_out));
  Multiplexer multiplexer_2 (.sel(B), .in_0(T3), .in_1(T4), .out(multiplexer_2_out));
  Multiplexer multiplexer_3 (.sel(A), .in_0(multiplexer_1_out), .in_1(multiplexer_2_out), .out(F));
endmodule
