// Digital circuit mux_truth_2bit_midterm.dig as structural Verilog
module mux_truth_2bit_midterm (
  input  _1,
  input  _1_2,
  input  _0,
  input  _1_3,
  input  _1_4,
  input  _0_2,
  output F
);

  wire multiplexer_1_out, multiplexer_2_out;

  Multiplexer multiplexer_1 (.sel(_0_2), .in_0(_1), .in_1(_1_2), .out(multiplexer_1_out));
  Multiplexer multiplexer_2 (.sel(_0_2), .in_0(_0), .in_1(_1_3), .out(multiplexer_2_out));
  Multiplexer multiplexer_3 (.sel(_1_4), .in_0(multiplexer_1_out), .in_1(multiplexer_2_out), .out(F));
endmodule
