// Digital circuit mux_truth_3bit.dig as structural Verilog
module mux_truth_3bit (
  input  T1,
  input  T2,
  input  T3,
  input  T4,
  input  X,
  input  Y,
  input  T5,
  input  T6,
  input  T7,
  input  T8,
  input  Z,
  output S
);

  wire multiplexer_1_out, multiplexer_2_out, multiplexer_3_out, multiplexer_4_out, multiplexer_5_out,
       multiplexer_6_out;

  Multiplexer multiplexer_1 (.sel(Z), .in_0(T1), .in_1(T2), .out(multiplexer_1_out));
  Multiplexer multiplexer_2 (.sel(Z), .in_0(T3), .in_1(T4), .out(multiplexer_2_out));
  Multiplexer multiplexer_3 (.sel(Z), .in_0(T5), .in_1(T6), .out(multiplexer_3_out));
  Multiplexer multiplexer_4 (.sel(Z), .in_0(T7), .in_1(T8), .out(multiplexer_4_out));
  Multiplexer multiplexer_5 (.sel(Y), .in_0(multiplexer_1_out), .in_1(multiplexer_2_out), .out(multiplexer_5_out));
  Multiplexer multiplexer_6 (.sel(Y), .in_0(multiplexer_3_out), .in_1(multiplexer_4_out), .out(multiplexer_6_out));
  Multiplexer multiplexer_7 (.sel(X), .in_0(multiplexer_5_out), .in_1(multiplexer_6_out), .out(S));
endmodule
