// Digital circuit mux_truth_3bit_midterm.dig as structural Verilog
module mux_truth_3bit_midterm (
  input  _1,
  input  _1_2,
  input  _0,
  input  _1_3,
  input  X,
  input  Y,
  input  _0_2,
  input  _0_3,
  input  _1_4,
  input  _1_5,
  input  Z,
  output S
);

  wire multiplexer_1_out, multiplexer_2_out, multiplexer_3_out, multiplexer_4_out, multiplexer_5_out,
       multiplexer_6_out;

  Multiplexer multiplexer_1 (.sel(Z), .in_0(_1), .in_1(_1_2), .out(multiplexer_1_out));
  Multiplexer multiplexer_2 (.sel(Z), .in_0(_0), .in_1(_1_3), .out(multiplexer_2_out));
  Multiplexer multiplexer_3 (.sel(Z), .in_0(_0_2), .in_1(_0_3), .out(multiplexer_3_out));
  Multiplexer multiplexer_4 (.sel(Z), .in_0(_1_4), .in_1(_1_5), .out(multiplexer_4_out));
  Multiplexer multiplexer_5 (.sel(Y), .in_0(multiplexer_1_out), .in_1(multiplexer_2_out), .out(multiplexer_5_out));
  Multiplexer multiplexer_6 (.sel(Y), .in_0(multiplexer_3_out), .in_1(multiplexer_4_out), .out(multiplexer_6_out));
  Multiplexer multiplexer_7 (.sel(X), .in_0(multiplexer_5_out), .in_1(multiplexer_6_out), .out(S));
endmodule
