// Digital circuit ram.dig as structural Verilog
module ram (
  input  [1:0] A,
  input  [3:0] D,
  input  wr,
  output [3:0] Q
);

  RAMAsync #(.Bits(4)) ramasync_1 (.A(A), .D(D), .we(wr), .Q(Q));
endmodule
