// Digital circuit ring_counter.dig as structural Verilog
module ring_counter (
  input  clk,
  output Q0,
  output Q1,
  output Q2,
  output Q3
);

  wire d_ff_4_nq;

  D_FF d_ff_1 (.D(d_ff_4_nq), .C(clk), .Q(Q0));  // open: nQ
  D_FF d_ff_2 (.D(Q0), .C(clk), .Q(Q1));  // open: nQ
  D_FF d_ff_3 (.D(Q1), .C(clk), .Q(Q2));  // open: nQ
  D_FF d_ff_4 (.D(Q2), .C(clk), .Q(Q3), .nQ(d_ff_4_nq));
endmodule
