// Digital circuit rom_2x4.dig as structural Verilog
module rom_2x4 (
  input  [1:0] Address,
  input  Logic0,
  output F3,
  output F2,
  output F1,
  output F0
);

  wire decoder_1_out_0, decoder_1_out_1, decoder_1_out_2, decoder_1_out_3;

  Decoder #(.Selector_Bits(2)) decoder_1 (
    .sel(Address), .out_0(decoder_1_out_0), .out_1(decoder_1_out_1), .out_2(decoder_1_out_2),
    .out_3(decoder_1_out_3));
  or or_1 (F3, decoder_1_out_3, decoder_1_out_2, Logic0, Logic0);
  or or_2 (F2, decoder_1_out_3, decoder_1_out_2, decoder_1_out_1, Logic0);
  or or_3 (F1, decoder_1_out_3, Logic0, decoder_1_out_1, decoder_1_out_0);
  or or_4 (F0, decoder_1_out_3, Logic0, Logic0, decoder_1_out_0);
endmodule
