// Digital circuit rom_halfadder.dig as structural Verilog
module rom_halfadder (
  input  [1:0] Address,
  input  Logic0,
  output C,
  output S
);

  wire decoder_1_out_0, decoder_1_out_1, decoder_1_out_2, decoder_1_out_3;

  Decoder #(.Selector_Bits(2)) decoder_1 (
    .sel(Address), .out_0(decoder_1_out_0), .out_1(decoder_1_out_1), .out_2(decoder_1_out_2),
    .out_3(decoder_1_out_3));
  or or_1 (C, decoder_1_out_3, Logic0, Logic0, Logic0);
  or or_2 (S, Logic0, decoder_1_out_2, decoder_1_out_1, Logic0);

  // Notes on the sheet:
  //   A:CS
  //   00:00
  //   01:01
  //   10:01
  //   11:10
endmodule
