// Digital circuit shannon_v2.dig as structural Verilog
module shannon_v2 (
  input  S,
  input  V,
  input  W,
  input  X,
  input  Y,
  input  Z,
  output F
);

  wire and_1_out, and_2_out, and_3_out, not_1_out, not_2_out, not_3_out, or_1_out, or_2_out, or_3_out,
       or_4_out;

  not not_1 (not_1_out, S);
  not not_2 (not_2_out, W);
  not not_3 (not_3_out, Z);
  or or_1 (or_1_out, S, not_2_out, Z);
  and and_1 (and_1_out, not_1_out, V);
  or or_2 (or_2_out, X, Z);
  or or_3 (or_3_out, X, Y);
  or or_4 (or_4_out, and_1_out, Y, not_3_out);
  and and_2 (and_2_out, not_2_out, or_3_out);
  and and_3 (and_3_out, or_1_out, or_4_out, or_2_out);
  or or_5 (F, and_3_out, W, and_2_out);
endmodule
