// Digital circuit shiftregister_parallel_out.dig as structural Verilog
module shiftregister_parallel_out (
  input  Si,
  input  clk,
  output So,
  output Q4,
  output Q3,
  output Q2,
  output Q1
);

  wire d_ff_1_nq, d_ff_1_q, d_ff_2_nq, d_ff_2_q, d_ff_3_nq, d_ff_3_q, d_ff_4_nq;

  D_FF d_ff_1 (.D(Si), .C(clk), .Q(d_ff_1_q), .nQ(d_ff_1_nq));
  D_FF d_ff_2 (.D(d_ff_1_q), .C(clk), .Q(d_ff_2_q), .nQ(d_ff_2_nq));
  not not_1 (Q1, d_ff_1_nq);
  not not_2 (Q2, d_ff_2_nq);
  D_FF d_ff_3 (.D(d_ff_2_q), .C(clk), .Q(d_ff_3_q), .nQ(d_ff_3_nq));
  D_FF d_ff_4 (.D(d_ff_3_q), .C(clk), .Q(So), .nQ(d_ff_4_nq));
  not not_3 (Q3, d_ff_3_nq);
  not not_4 (Q4, d_ff_4_nq);
endmodule
