// Digital circuit sn74f283.dig as structural Verilog
module sn74f283 (
  input  B,
  input  A,
  input  C,
  output S
);

  wire and_1_out, nand_1_out, nor_1_out, not_1_out, not_2_out, not_3_out;

  nand nand_1 (nand_1_out, B, A);
  nor nor_1 (nor_1_out, B, A);
  not not_1 (not_1_out, C);
  not not_2 (not_2_out, nor_1_out);
  and and_1 (and_1_out, nand_1_out, not_2_out);
  not not_3 (not_3_out, not_1_out);
  xor xor_1 (S, and_1_out, not_3_out);
endmodule
