// Digital circuit sn74f283_V2.dig as structural Verilog
module sn74f283_V2 (
  input  B,
  input  A,
  input  C,
  output S
);

  wire and_1_out, and_2_out, and_3_out, and_4_out, not_1_out, not_2_out, not_3_out;

  not not_1 (not_1_out, B);
  not not_2 (not_2_out, A);
  not not_3 (not_3_out, C);
  and and_1 (and_1_out, not_2_out, not_1_out, C);
  and and_2 (and_2_out, A, not_1_out, not_3_out);
  and and_3 (and_3_out, not_2_out, B, not_3_out);
  and and_4 (and_4_out, A, B, C);
  or or_1 (S, and_1_out, and_2_out, and_3_out, and_4_out);
endmodule
