// Digital circuit two_to_four_decoder_enable_V2.dig as structural Verilog
module two_to_four_decoder_enable_V2 (
  input  A,
  input  B,
  input  E,
  output D0,
  output D1,
  output D2,
  output D3
);

  wire not_1_out, not_2_out, not_3_out;

  not not_1 (not_1_out, E);
  not not_2 (not_2_out, A);
  not not_3 (not_3_out, B);
  nand nand_1 (D0, not_2_out, not_3_out, not_1_out);
  nand nand_2 (D1, not_2_out, B, not_1_out);
  nand nand_3 (D2, A, not_3_out, not_1_out);
  nand nand_4 (D3, A, B, not_1_out);
endmodule
