// Digital circuit verilog_primitives2.dig as structural Verilog
module verilog_primitives2 (
  input  A,
  input  B,
  input  C,
  output D,
  output W1
);

  wire and_1_out;

  and and_1 (and_1_out, A, B);
  and and_2 (D, and_1_out, C);
endmodule
