// Digital circuit writemyname_example.dig as structural Verilog
module writemyname_example (
  input  btn
);

  wire and_1_out, nand_1_out, nor_1_out, not_1_out, xnor_1_out, xor_1_out;

  xor xor_1 (xor_1_out, btn, btn);
  and and_1 (and_1_out, btn, 1'b1);
  nand nand_1 (nand_1_out, btn, 1'b1);
  nor nor_1 (nor_1_out, 1'b1, 1'b0);
  xnor xnor_1 (xnor_1_out, 1'b0, 1'b1);
  not not_1 (not_1_out, 1'b0);
  Seven_Seg seven_seg_1 (
    .a(xor_1_out), .b(and_1_out), .c(nand_1_out), .d(nor_1_out), .e(xnor_1_out), .f(xnor_1_out),
    .g(not_1_out), .dp(1'b0));
endmodule
