// Digital circuit xy.dig as structural Verilog
module xy (
  input  x,
  input  y_2,
  output Y
);

  wire not_1_out, or_1_out;

  not not_1 (not_1_out, x);
  or or_1 (or_1_out, not_1_out, y_2);
  and and_1 (Y, x, or_1_out);
endmodule
